// Logisim project RiscV.circ as structural Verilog: 12 circuits, main circuit main
module main (
  input  [31:0] in_1
);

  wire alu_ctrl_1_alu_src, clock_1_out;
  wire [3:0] alu_ctrl_1_ctrl_0;
  wire [31:0] bit_extender_1_out, multiplexer_1_out, reg_file_1_rdata1, reg_file_1_rdata2,
       thirty_two_bit_alu_1_r;

  Clock clock_1 (.out(clock_1_out));
  assign bit_extender_1_out = {{20{in_1[31]}}, in_1[31:20]};  // Bit_Extender bit_extender_1
  reg_file reg_file_1 (
    .WData(thirty_two_bit_alu_1_r), .RReg1(in_1[19:15]), .WReg(in_1[11:7]), .RReg2(in_1[24:20]),
    .Write(1'b1), .CLK_In(clock_1_out), .RDATA1(reg_file_1_rdata1), .RDATA2(reg_file_1_rdata2));
  ALU_CTRL alu_ctrl_1 (
    .i30(in_1[30]), .i14(in_1[14]), .i13(in_1[13]), .i12(in_1[12]), .i6(in_1[6]), .i5(in_1[5]), .i4(in_1[4]),
    .CTRL_3(alu_ctrl_1_ctrl_0[3]), .CTRL_2(alu_ctrl_1_ctrl_0[2]), .CTRL_1(alu_ctrl_1_ctrl_0[1]),
    .CTRL_0(alu_ctrl_1_ctrl_0[0]), .ALU_SRC(alu_ctrl_1_alu_src));
  Multiplexer #(.enable("false"), .width(32)) multiplexer_1 (
    .in0(reg_file_1_rdata2), .in1(bit_extender_1_out), .out(multiplexer_1_out), .sel(alu_ctrl_1_alu_src));
  thirty_two_bit_ALU thirty_two_bit_alu_1 (
    .in_1(alu_ctrl_1_ctrl_0), .A(reg_file_1_rdata1), .B(multiplexer_1_out), .R(thirty_two_bit_alu_1_r));  // open: C_out
endmodule

module ASU (
  input  [3:0] ASU_ctrl,
  input  A,
  input  B,
  input  C_IN,
  output R,
  output C_OUT
);

  wire and_1_out, multiplexer_1_out, not_1_out, one_bit_adder_1_out_4, or_1_out, xor_1_out;

  not not_1 (not_1_out, B);
  Multiplexer #(.enable("false")) multiplexer_1 (.in0(B), .in1(not_1_out), .out(multiplexer_1_out), .sel(ASU_ctrl[2]));
  and and_1 (and_1_out, A, multiplexer_1_out);
  or or_1 (or_1_out, A, multiplexer_1_out);
  xor xor_1 (xor_1_out, multiplexer_1_out, A);
  one_BIT_adder one_bit_adder_1 (
    .A(A), .B(multiplexer_1_out), .C_in(C_IN), .out_4(one_bit_adder_1_out_4), .C_out(C_OUT));
  Multiplexer #(.enable("false"), .select(2)) multiplexer_2 (
    .in0(and_1_out), .in1(or_1_out), .in2(xor_1_out), .in3(one_bit_adder_1_out_4), .out(R),
    .sel(ASU_ctrl[1:0]));
endmodule

module one_BIT_adder (
  input  A,
  input  B,
  input  C_in,
  output out_4,
  output C_out
);

  wire and_1_out, and_2_out, xor_1_out;

  xor xor_1 (xor_1_out, A, B);
  and and_1 (and_1_out, A, B);
  xor xor_2 (out_4, xor_1_out, C_in);
  and and_2 (and_2_out, xor_1_out, C_in);
  or or_1 (C_out, and_2_out, and_1_out);
endmodule

module EightBitALU (
  input  [3:0] ASU_CTRL,
  input  [7:0] A,
  input  [7:0] B,
  input  C_IN,
  output [7:0] Results,
  output C_out
);

  wire asu_1_c_out, asu_2_c_out, asu_3_c_out, asu_4_c_out, asu_5_c_out, asu_6_c_out, asu_7_c_out;

  ASU asu_1 (.ASU_ctrl(ASU_CTRL), .A(A[0]), .B(B[0]), .C_IN(C_IN), .R(Results[0]), .C_OUT(asu_1_c_out));
  ASU asu_2 (.ASU_ctrl(ASU_CTRL), .A(A[1]), .B(B[1]), .C_IN(asu_1_c_out), .R(Results[1]), .C_OUT(asu_2_c_out));
  ASU asu_3 (.ASU_ctrl(ASU_CTRL), .A(A[2]), .B(B[2]), .C_IN(asu_2_c_out), .R(Results[2]), .C_OUT(asu_3_c_out));
  ASU asu_4 (.ASU_ctrl(ASU_CTRL), .A(A[3]), .B(B[3]), .C_IN(asu_3_c_out), .R(Results[3]), .C_OUT(asu_4_c_out));
  ASU asu_5 (.ASU_ctrl(ASU_CTRL), .A(A[4]), .B(B[4]), .C_IN(asu_4_c_out), .R(Results[4]), .C_OUT(asu_5_c_out));
  ASU asu_6 (.ASU_ctrl(ASU_CTRL), .A(A[5]), .B(B[5]), .C_IN(asu_5_c_out), .R(Results[5]), .C_OUT(asu_6_c_out));
  ASU asu_7 (.ASU_ctrl(ASU_CTRL), .A(A[6]), .B(B[6]), .C_IN(asu_6_c_out), .R(Results[6]), .C_OUT(asu_7_c_out));
  ASU asu_8 (.ASU_ctrl(ASU_CTRL), .A(A[7]), .B(B[7]), .C_IN(asu_7_c_out), .R(Results[7]), .C_OUT(C_out));
endmodule

module thirty_two_bit_ALU (
  input  [3:0] in_1,
  input  [31:0] A,
  input  [31:0] B,
  output [31:0] R,
  output C_out
);

  wire eightbitalu_1_c_out, eightbitalu_2_c_out, eightbitalu_3_c_out;

  EightBitALU eightbitalu_1 (
    .ASU_CTRL(in_1), .A(A[7:0]), .B(B[7:0]), .C_IN(in_1[2]), .Results(R[7:0]), .C_out(eightbitalu_1_c_out));
  EightBitALU eightbitalu_2 (
    .ASU_CTRL(in_1), .A(A[15:8]), .B(B[15:8]), .C_IN(eightbitalu_1_c_out), .Results(R[15:8]),
    .C_out(eightbitalu_2_c_out));
  EightBitALU eightbitalu_3 (
    .ASU_CTRL(in_1), .A(A[23:16]), .B(B[23:16]), .C_IN(eightbitalu_2_c_out), .Results(R[23:16]),
    .C_out(eightbitalu_3_c_out));
  EightBitALU eightbitalu_4 (
    .ASU_CTRL(in_1), .A(A[31:24]), .B(B[31:24]), .C_IN(eightbitalu_3_c_out), .Results(R[31:24]), .C_out(C_out));
endmodule

module reg_file (
  input  [31:0] WData,
  input  [4:0] RReg1,
  input  [4:0] WReg,
  input  [4:0] RReg2,
  input  Write,
  input  CLK_In,
  output [31:0] RDATA1,
  output [31:0] RDATA2
);

  wire R0, R1, R2, R3, R4, R5, R6, R7, R8, R9, R10, R11, R12, R13, R14, R15, R16, R17, R18, R19, R20, R21,
       R22, R23, R24, R25, R26, R27, R28, R29, R30, R31;
  wire [31:0] Q0, Q1, Q2, Q3, Q4, Q5, Q6, Q7, Q8, Q9, Q10, Q11, Q12, Q13, Q14, Q15, Q16, Q17, Q18, Q19, Q20,
       Q21, Q22, Q23, Q24, Q25, Q26, Q27, Q28, Q29, Q30, Q31;

  Demultiplexer #(.enable("false"), .select(5)) demultiplexer_1 (
    .out0(R0), .out1(R1), .out2(R2), .out3(R3), .out4(R4), .out5(R5), .out6(R6), .out7(R7), .out8(R8),
    .out9(R9), .out10(R10), .out11(R11), .out12(R12), .out13(R13), .out14(R14), .out15(R15), .out16(R16),
    .out17(R17), .out18(R18), .out19(R19), .out20(R20), .out21(R21), .out22(R22), .out23(R23), .out24(R24),
    .out25(R25), .out26(R26), .out27(R27), .out28(R28), .out29(R29), .out30(R30), .out31(R31), .in(Write),
    .sel(WReg));
  Register #(.width(32)) register_1 (.D(WData), .en(R0), .clk(CLK_In), .Q(Q0), .clr(Write));
  Register #(.width(32)) register_2 (.D(WData), .en(R1), .clk(CLK_In), .Q(Q1));  // open: clr
  Register #(.width(32)) register_3 (.en(R2), .clk(CLK_In), .Q(Q2));  // open: D, clr
  Register #(.width(32)) register_4 (.D(WData), .en(R3), .clk(CLK_In), .Q(Q3));  // open: clr
  Register #(.width(32)) register_5 (.D(WData), .en(R4), .clk(CLK_In), .Q(Q4));  // open: clr
  Register #(.width(32)) register_6 (.D(WData), .en(R5), .clk(CLK_In), .Q(Q5));  // open: clr
  Register #(.width(32)) register_7 (.D(WData), .en(R6), .clk(CLK_In), .Q(Q6));  // open: clr
  Register #(.width(32)) register_8 (.D(WData), .en(R7), .clk(CLK_In), .Q(Q7));  // open: clr
  Register #(.width(32)) register_9 (.D(WData), .en(R8), .clk(CLK_In), .Q(Q8));  // open: clr
  Register #(.width(32)) register_10 (.D(WData), .en(R9), .clk(CLK_In), .Q(Q9));  // open: clr
  Register #(.width(32)) register_11 (.D(WData), .en(R10), .clk(CLK_In), .Q(Q10));  // open: clr
  Register #(.width(32)) register_12 (.D(WData), .en(R11), .clk(CLK_In), .Q(Q11), .clr(Write));
  Register #(.width(32)) register_13 (.D(WData), .en(R12), .clk(CLK_In), .Q(Q12));  // open: clr
  Register #(.width(32)) register_14 (.D(WData), .en(R13), .clk(CLK_In), .Q(Q13));  // open: clr
  Register #(.width(32)) register_15 (.D(WData), .en(R14), .clk(CLK_In), .Q(Q14));  // open: clr
  Register #(.width(32)) register_16 (.D(WData), .en(R15), .clk(CLK_In), .Q(Q15));  // open: clr
  Register #(.width(32)) register_17 (.D(WData), .en(R16), .clk(CLK_In), .Q(Q16));  // open: clr
  Register #(.width(32)) register_18 (.D(WData), .en(R17), .clk(CLK_In), .Q(Q17));  // open: clr
  Register #(.width(32)) register_19 (.D(WData), .en(R18), .clk(CLK_In), .Q(Q18));  // open: clr
  Register #(.width(32)) register_20 (.D(WData), .en(R19), .clk(CLK_In), .Q(Q19));  // open: clr
  Register #(.width(32)) register_21 (.D(WData), .en(R20), .clk(CLK_In), .Q(Q20));  // open: clr
  Register #(.width(32)) register_22 (.D(WData), .en(R21), .clk(CLK_In), .Q(Q21));  // open: clr
  Register #(.width(32)) register_23 (.D(WData), .en(R22), .clk(CLK_In), .Q(Q22));  // open: clr
  Register #(.width(32)) register_24 (.D(WData), .en(R23), .clk(CLK_In), .Q(Q23));  // open: clr
  Register #(.width(32)) register_25 (.D(WData), .en(R24), .clk(CLK_In), .Q(Q24));  // open: clr
  Register #(.width(32)) register_26 (.D(WData), .en(R25), .clk(CLK_In), .Q(Q25));  // open: clr
  Register #(.width(32)) register_27 (.D(WData), .en(R26), .clk(CLK_In), .Q(Q26));  // open: clr
  Register #(.width(32)) register_28 (.D(WData), .en(R27), .clk(CLK_In), .Q(Q27));  // open: clr
  Register #(.width(32)) register_29 (.D(WData), .en(R28), .clk(CLK_In), .Q(Q28));  // open: clr
  Register #(.width(32)) register_30 (.D(WData), .en(R29), .clk(CLK_In), .Q(Q29));  // open: clr
  Register #(.width(32)) register_31 (.D(WData), .en(R30), .clk(CLK_In), .Q(Q30));  // open: clr
  Register #(.width(32)) register_32 (.D(WData), .en(R31), .clk(CLK_In), .Q(Q31));  // open: clr
  Multiplexer #(.enable("false"), .select(5), .width(32)) multiplexer_1 (
    .in0(Q0), .in1(Q1), .in2(Q2), .in3(Q3), .in4(Q4), .in5(Q5), .in6(Q6), .in7(Q7), .in8(Q8), .in9(Q9),
    .in10(Q10), .in11(Q11), .in12(Q12), .in13(Q13), .in14(Q14), .in15(Q15), .in16(Q16), .in17(Q17),
    .in18(Q18), .in19(Q19), .in20(Q20), .in21(Q21), .in22(Q22), .in23(Q23), .in24(Q24), .in25(Q25),
    .in26(Q26), .in27(Q27), .in28(Q28), .in29(Q29), .in30(Q30), .in31(Q31), .out(RDATA1), .sel(RReg1));
  Multiplexer #(.enable("false"), .select(5), .width(32)) multiplexer_2 (
    .in0(Q0), .in1(Q1), .in2(Q2), .in3(Q3), .in4(Q4), .in5(Q5), .in6(Q6), .in7(Q7), .in8(Q8), .in9(Q9),
    .in10(Q10), .in11(Q11), .in12(Q12), .in13(Q13), .in14(Q14), .in15(Q15), .in16(Q16), .in17(Q17),
    .in18(Q18), .in19(Q19), .in20(Q20), .in21(Q21), .in22(Q22), .in23(Q23), .in24(Q24), .in25(Q25),
    .in26(Q26), .in27(Q27), .in28(Q28), .in29(Q29), .in30(Q30), .in31(Q31), .out(RDATA2), .sel(RReg2));

  // Other names for the same wires on the sheet: CLK = CLK_In; W = Write
endmodule

module ALU_CTRL (
  input  i30,
  input  i14,
  input  i13,
  input  i12,
  input  i6,
  input  i5,
  input  i4,
  output CTRL_3,
  output CTRL_2,
  output CTRL_1,
  output CTRL_0,
  output ALU_SRC
);

  wire and_1_out, and_2_out, and_3_out, and_4_out, and_5_out, not_1_out, not_2_out, not_3_out, not_4_out,
       not_5_out, not_6_out;

  not not_1 (not_1_out, i14);
  not not_2 (not_2_out, i13);
  not not_3 (not_3_out, i12);
  not not_4 (not_4_out, i6);
  not not_5 (not_5_out, i5);
  not not_6 (not_6_out, i4);
  and and_1 (and_1_out, not_1_out, not_3_out, not_4_out, not_6_out);
  and and_2 (and_2_out, i13, not_3_out);
  and and_3 (and_3_out, not_2_out, not_3_out, not_4_out, not_5_out, i4);
  and and_4 (and_4_out, not_1_out, i13, not_3_out, not_4_out, not_6_out);
  and and_5 (and_5_out, i14, i13, not_4_out, not_5_out, i4);
  or or_1 (CTRL_1, and_1_out, not_2_out);
  or or_2 (CTRL_0, not_1_out, and_2_out);
  or or_3 (ALU_SRC, and_3_out, and_4_out, and_5_out);

  assign CTRL_2 = 1'b0;
  assign CTRL_3 = 1'b0;
endmodule

module Imm_Gen (
  input  [31:0] in_1,
  output [31:0] out_2
);

  Multiplexer #(.enable("false")) multiplexer_1 (.in0(in_1[31]), .in1(in_1[7]), .out(out_2[11]), .sel(in_1[6]));
  Multiplexer #(.enable("false"), .width(4)) multiplexer_2 (
    .in0(in_1[24:21]), .in1(in_1[11:8]), .out(out_2[4:1]), .sel(in_1[5]));
  assign out_2[31:12] = {{19{in_1[31]}}, in_1[31]};  // Bit_Extender bit_extender_1
  Multiplexer #(.enable("false"), .select(2)) multiplexer_3 (
    .in0(in_1[20]), .in1(in_1[7]), .in3(1'b0), .out(out_2[0]), .sel(in_1[6:5]));  // open: in2

  assign out_2[10:5] = in_1[30:25];

  // Other names for the same wires on the sheet: I5 = in_1[5]; I6_5[1:0] = in_1[6:5]; I6 = in_1[6]; I7 = in_1[7];
  //   I11_8[3:0] = in_1[11:8]; I_20 = in_1[20]; I24_21[3:0] = in_1[24:21]; I_31 = in_1[31]; I30_25[5:0] = in_1[30:25]
endmodule

module Instruction_memory (
  input  [23:0] Address,
  input  Clock_in,
  output [31:0] Instruction
);

  wire not_1_out;

  not not_1 (not_1_out, Clock_in);
  RAM #(.addrWidth(22), .asyncread("true"), .dataWidth(32)) ram_1 (
    .addr(Address[23:2]), .we(1'b0), .oe(not_1_out), .dout(Instruction));  // open: clk, din
endmodule

module Data_memory (
  input  [25:0] Address,
  input  MemWrite,
  input  MemRead,
  input  ClkIn,
  input  [31:0] WriteData,
  output [31:0] out_6
);

  RAM #(.addrWidth(24), .asyncread("true"), .dataWidth(32)) ram_1 (
    .addr(Address[25:2]), .we(MemWrite), .oe(MemRead), .clk(ClkIn), .din(WriteData), .dout(out_6));
endmodule

module Control (
  input  [6:0] I0_I6,
  output Memtoreg,
  output regwrite,
  output memread,
  output memwrite,
  output branch
);

  wire not_1_out, not_2_out, not_3_out;

  not not_1 (not_1_out, I0_I6[6]);
  not not_2 (not_2_out, I0_I6[5]);
  not not_3 (not_3_out, I0_I6[4]);
  and and_1 (Memtoreg, not_2_out, not_3_out);
  or or_1 (regwrite, not_2_out, I0_I6[4]);
  and and_2 (memread, not_2_out, not_3_out);
  and and_3 (memwrite, not_1_out, I0_I6[5], not_3_out);

  assign branch = I0_I6[6];
endmodule

module RiscV (
);

  wire alu_ctrl_1_alu_src, and_1_out, clock_1_out, comparator_1_eq, control_1_branch, control_1_memread,
       control_1_memtoreg, control_1_memwrite, control_1_regwrite;
  wire [3:0] alu_ctrl_1_ctrl_0;
  wire [6:0] instruction_memory_1_instruction;
  wire [25:0] R;
  wire [31:0] adder_1_out, adder_2_out, data_memory_1_out_6, imm_gen_1_out_2, multiplexer_1_out,
       multiplexer_2_out, multiplexer_3_out, reg_file_1_rdata1, reg_file_1_rdata2, register_1_q;
  wire [31:7] instruction_memory_1_instruction_2;
  wire [31:26] thirty_two_bit_alu_1_r;

  Register #(.width(32)) register_1 (
    .D(multiplexer_1_out), .en(1'b1), .clk(clock_1_out), .Q(register_1_q));  // open: clr
  Clock clock_1 (.out(clock_1_out));
  Adder #(.width(32)) adder_1 (.a(register_1_q), .b(32'h4), .out(adder_1_out));  // open: cin, cout
  Instruction_memory instruction_memory_1 (
    .Address(register_1_q[23:0]), .Clock_in(clock_1_out),
    .Instruction({instruction_memory_1_instruction_2, instruction_memory_1_instruction}));
  Control control_1 (
    .I0_I6(instruction_memory_1_instruction), .Memtoreg(control_1_memtoreg), .regwrite(control_1_regwrite),
    .memread(control_1_memread), .memwrite(control_1_memwrite), .branch(control_1_branch));
  Adder #(.width(32)) adder_2 (.a(register_1_q), .b(imm_gen_1_out_2), .out(adder_2_out));  // open: cin, cout
  Imm_Gen imm_gen_1 (
    .in_1({instruction_memory_1_instruction_2, instruction_memory_1_instruction}), .out_2(imm_gen_1_out_2));
  Multiplexer #(.enable("false"), .width(32)) multiplexer_1 (
    .in0(adder_1_out), .in1(adder_2_out), .out(multiplexer_1_out), .sel(and_1_out));
  ALU_CTRL alu_ctrl_1 (
    .i30(instruction_memory_1_instruction_2[30]), .i14(instruction_memory_1_instruction_2[14]),
    .i13(instruction_memory_1_instruction_2[13]), .i12(instruction_memory_1_instruction_2[12]),
    .i6(instruction_memory_1_instruction[6]), .i5(instruction_memory_1_instruction[5]),
    .i4(instruction_memory_1_instruction[4]), .CTRL_3(alu_ctrl_1_ctrl_0[3]), .CTRL_2(alu_ctrl_1_ctrl_0[2]),
    .CTRL_1(alu_ctrl_1_ctrl_0[1]), .CTRL_0(alu_ctrl_1_ctrl_0[0]), .ALU_SRC(alu_ctrl_1_alu_src));
  reg_file reg_file_1 (
    .WData(multiplexer_3_out), .RReg1(instruction_memory_1_instruction_2[19:15]),
    .WReg(instruction_memory_1_instruction_2[11:7]), .RReg2(instruction_memory_1_instruction_2[24:20]),
    .Write(control_1_regwrite), .CLK_In(clock_1_out), .RDATA1(reg_file_1_rdata1), .RDATA2(reg_file_1_rdata2));
  Comparator #(.width(32)) comparator_1 (
    .a(reg_file_1_rdata1), .b(reg_file_1_rdata2), .eq(comparator_1_eq));  // open: gt, lt
  Multiplexer #(.enable("false"), .width(32)) multiplexer_2 (
    .in0(reg_file_1_rdata2), .in1(imm_gen_1_out_2), .out(multiplexer_2_out), .sel(alu_ctrl_1_alu_src));
  and and_1 (and_1_out, control_1_branch, comparator_1_eq);
  Data_memory data_memory_1 (
    .Address(R), .MemWrite(control_1_memwrite), .MemRead(control_1_memread), .ClkIn(clock_1_out),
    .WriteData(reg_file_1_rdata2), .out_6(data_memory_1_out_6));
  thirty_two_bit_ALU thirty_two_bit_alu_1 (
    .in_1(alu_ctrl_1_ctrl_0), .A(reg_file_1_rdata1), .B(multiplexer_2_out), .R({thirty_two_bit_alu_1_r, R}));  // open: C_out
  Multiplexer #(.enable("false"), .width(32)) multiplexer_3 (
    .in0({thirty_two_bit_alu_1_r, R}), .in1(data_memory_1_out_6), .out(multiplexer_3_out),
    .sel(control_1_memtoreg));
endmodule
